# Fritzing sketch esquema_electronico_KjPeJoo7X9 (saved by Fritzing 0.9.3b)
breadboards: 1

parts:
  U2 = RELAY [package=relay-g5q]
  U3 = RELAY [package=relay-g5q]
  U4 = RELAY [package=relay-g5q]
  U5 = RELAY [package=relay-g5q]
  Q1 = NPN-Transistor [package="TO92 [THT]"]
  Q2 = NPN-Transistor [package="TO92 [THT]"]
  Q3 = NPN-Transistor [package="TO92 [THT]"]
  Q4 = NPN-Transistor [package="TO92 [THT]"]
  D1 = Diode [package=diode-1n4001]
  D2 = Diode [package=diode-1n4001]
  D3 = Diode [package=diode-1n4001]
  D4 = Diode [package=diode-1n4001]
  R1 = Resistor [tolerance=±5% resistance=1k package="2010 [SMD]"]
  J1 = Camdenboss CTB0158-2 [part_number=CTB0158-2 package=THT]
  J2 = Camdenboss CTB0158-3 [part_number=CTB0158-3 package=THT]
  J3 = Camdenboss CTB0158-2 [part_number=CTB0158-2 package=THT]
  J4 = Camdenboss CTB0158-2 [part_number=CTB0158-2 package=THT]
  J5 = Camdenboss CTB0158-2 [part_number=CTB0158-2 package=THT]
  R2 = Resistor [tolerance=±5% resistance=1k package="2010 [SMD]"]
  R3 = Resistor [tolerance=±5% resistance=1k package="2010 [SMD]"]
  R4 = Resistor [tolerance=±5% resistance=1k package="2010 [SMD]"]
  U1 = NodeMCU V1.0
  T1 = LM35 Temperature Sensor [package="TO92 [THT]"]
  PIR1 = PIR sensor
  U6 = RELAY [package=relay-g5q]
  U7 = RELAY [package=relay-g5q]
  D5 = Diode [package=diode-1n4001]
  D6 = Diode [package=diode-1n4001]
  Q5 = NPN-Transistor [package="TO92 [THT]"]
  Q6 = NPN-Transistor [package="TO92 [THT]"]
  R5 = Resistor [tolerance=±5% resistance=1k package="2010 [SMD]"]
  R6 = Resistor [tolerance=±5% resistance=1k package="2010 [SMD]"]
  J6 = Camdenboss CTB0158-2 [part_number=CTB0158-2 package=THT]
  J7 = Camdenboss CTB0158-2 [part_number=CTB0158-2 package=THT]
  S1 = SWITCH-MOMENTARY-2 [package=tactile-pth]
  S2 = SWITCH-MOMENTARY-2 [package=tactile-pth]
  J8 = Camdenboss CTB0158-2 [part_number=CTB0158-2 package=THT]
  M1 = DC Motor
  R7 = Resistor [tolerance=±5% resistance=10k package="2010 [SMD]"]
  R8 = Resistor [tolerance=±5% resistance=10k package="2010 [SMD]"]
  J9 = Camdenboss CTB0158-2 [part_number=CTB0158-2 package=THT]
  V1 = AC Power [voltage=110 frequency=60]
  M2 = DC Motor
  J10 = Camdenboss CTB0158-2 [part_number=CTB0158-2 package=THT]
  C2 = Film/Foil Capacitor [capacitance=100nF voltage=35V package="15mm [THT, pp]"]

nets:
  N1: U2.COIL2, Q1.C, D1.A
  N2: U2.MAIN, J3.pin2
  N3: U2.NO, J3.pin1
  N4: U2.COIL1, U3.COIL1, U4.COIL1, U5.COIL1, D1.C, D2.C, D3.C, D4.C, U1.VV, T1.+Vs, PIR1.VDD
  N5: U3.COIL2, Q2.C, D2.A
  N6: U3.MAIN, U4.NO
  N7: U3.NO, J2.pin2
  N8: U3.NC, J2.pin1
  N9: U4.COIL2, Q3.C, D3.A
  N10: U4.MAIN, U5.MAIN, J1.pin1, J2.pin3
  N11: U5.COIL2, Q4.C, D4.A
  N12: U5.NO, J1.pin2
  GND: Q1.E, Q2.E, Q3.E, Q4.E, U1.GND, PIR1.GND
  N13: Q1.B, R1.Pin_1
  N14: Q2.B, R2.Pin_1
  N15: Q3.B, R3.Pin_1
  N16: Q4.B, R4.Pin_1
  N17: R1.Pin_0, U1.D3
  N18: J1.terminal_1, V1.V+
  N19: J1.terminal_2, J10.pin1
  N20: J2.terminal_1, C2.+
  N21: J2.terminal_2, M2.pin_1, C2.-
  N22: J4.pin1, U1.D4
  N23: J4.pin2, U1.D6
  N24: J4.terminal_1, J9.terminal_2
  N25: J4.terminal_2, J9.terminal_1
  N26: J5.pin2, U1.RSV, T1.GND
  GND_2: J5.terminal_2, J7.terminal_1
  N27: R2.Pin_0, U1.D2
  N28: R3.Pin_0, U1.D1
  N29: R4.Pin_0, U1.D0
  N30: U1.D5, PIR1.SIG
  N31: U1.A0, T1.Vout
  N32: U6.COIL2, D5.A, Q5.C
  N33: U6.MAIN, J8.pin1
  N34: U6.NO, U7.NO, J6.pin2
  N35: U6.NC, U7.NC, J6.pin1
  N36: U6.COIL1, D5.C, J7.pin2, S1.1, S2.1
  N37: U7.COIL2, D6.A, Q6.C
  N38: U7.MAIN, J8.pin2
  N39: U7.COIL1, D6.C
  N40: Q5.E, Q6.E, J7.pin1, R7.Pin_1, R8.Pin_1
  N41: Q5.B, R5.Pin_1
  N42: Q6.B, R6.Pin_1
  N43: R5.Pin_0, S1.2, R7.Pin_0, J9.pin2
  N44: R6.Pin_0, S2.2, R8.Pin_0, J9.pin1
  12V: J7.terminal_2
  N45: J8.terminal_1, M1.pin_1
  N46: J8.terminal_2, M1.pin_2
  N47: V1.V-, M2.pin_2, J10.pin2

notes:
  Lámpara
  Abanico
  Diseñado por Christopher Méndez
  @mcmchris

custom parts:
  NodeMCU V1.0: ESP8266 based NodeMCU
